# Fritzing sketch IOT nhom 1 (saved by Fritzing 1.0.6)
breadboards: 3

parts:
  Part2 = RFID-RC522-v2
  M1 = RioRand LM2596
  Part1 = Arduino Uno (Rev3)
  Mod1 = Amica NodeMCU DEVKIT 1.0
  VCC1 = 4 x AAA Battery Mount [internal_resistance=0.1Ω]
  J1 = Piezo Speaker
  M2 = Dagu DGServo 9g (Pan and tilt) [part_number=RS001B]
  LED1 = RGB LED (com. anode, rbg) [color="Red (633nm)" current=0.030A package="5 mm [THT]"]
  R1 = Resistor [tolerance=±5% power=0.25W resistance=220 package=THT]
  Part3 = Arduino Uno (Rev3)
  J2 = Piezo Speaker
  M3 = Dagu DGServo 9g (Pan and tilt) [part_number=RS001B]
  Part4 = RFID-RC522-v2
  Part5 = Arduino Uno (Rev3)
  J3 = Piezo Speaker
  M4 = Dagu DGServo 9g (Pan and tilt) [part_number=RS001B]
  Part6 = RFID-RC522-v2
  Mod2 = Amica NodeMCU DEVKIT 1.0

nets:
  N1: Part2.SDA, Part1.D10_PWM/SS
  N2: Part2.SCK, Part1.D13/SCK
  N3: Part2.MOSI, Part1.D11_PWM/MOSI
  N4: Part2.MISO, Part1.D12/MISO
  GND: Part2.GND, M1.Pin_4, Part1.GND, Mod1.pin_9, Mod1.pin_29, J1.pin1, M2.gnd, R1.Pin_0
  N5: Part2.RST, Part1.D9_PWM
  3.3V: Part2.3.3V, Part1.3V3
  N6: M1.Pin_1, VCC1.+
  N7: M1.Pin_2, VCC1.-
  VIN: M1.Pin_3, Part1.VIN, Mod1.pin_30, M2.vcc
  N8: Part1.D2, J1.pin2
  N9: Part1.D3_PWM, M2.pulse
  N10: Part1.D5_PWM, Mod1.pin4
  N11: Part1.D6_PWM, Mod1.pin3
  N12: Mod1.pin6, LED1.blue_cathode
  N13: Mod1.pin_13, LED1.green_cathode
  N14: Mod1.pin_14, LED1.red_cathode
  N15: LED1.common_anode, R1.Pin_1
  N16: Part3.D9_PWM, Part4.RST
  N17: Part3.D10_PWM/SS, Part4.SDA
  N18: Part3.D11_PWM/MOSI, Part4.MOSI
  N19: Part3.D12/MISO, Part4.MISO
  N20: Part3.D13/SCK, Part4.SCK
  N21: Part3.D2, J2.pin2
  N22: Part3.D3_PWM, M3.pulse
  5V: Part3.5V, M3.vcc, Part4.3.3V
  GND_2: Part3.GND, J2.pin1, M3.gnd, Part4.GND
  N23: Part5.D9_PWM, Part6.RST
  N24: Part5.D10_PWM/SS, Part6.SDA
  N25: Part5.D11_PWM/MOSI, Part6.MOSI
  N26: Part5.D12/MISO, Part6.MISO
  N27: Part5.D13/SCK, Part6.SCK
  N28: Part5.D2, J3.pin2
  N29: Part5.D3_PWM, M4.pulse
  N30: Part5.D5_PWM, Mod2.pin4
  N31: Part5.D6_PWM, Mod2.pin3
  3V3: Part5.3V3, Part6.3.3V
  GND_3: Part5.GND, J3.pin1, M4.gnd, Part6.GND, Mod2.pin_9, Mod2.pin_25, Mod2.pin_29
  VIN_2: Part5.VIN, M4.vcc, Mod2.pin_30

notes:
  SDA (purple) connect to ~D10
  SCK (brown) connect D13
  MOSI (orange) connect ~D11
  MISO (green) connect D12
  RST (yellow) connect ~D9
  RX (cyan) connect to ~D5
  TX (blue) connect to ~D6

custom parts:
  RFID-RC522-v2: A simple China made RFID-RC522 Reader; do check the pin labels, as this is a MFRC522 based clone.
